// Logisim project data path.circ as structural Verilog
module data_path (
  input  in_1,
  input  in_2,
  input  in_3,
  input  [1:0] in_4,
  input  in_5,
  input  in_6,
  input  [1:0] in_7,
  input  in_8
);

  wire clock_1_out;
  wire [7:0] AC_q, adder_1_out, AR_q, MAR_q, MBR_q, multiplexer_1_out, multiplexer_2_out, multiplexer_3_out,
       PC_q, ram_1_data;

  Clock clock_1 (.out(clock_1_out));
  Register AC (.D(adder_1_out), .en(in_1), .Q(AC_q), .clk(clock_1_out), .clr(in_8));
  Register PC (.D(adder_1_out), .en(in_3), .Q(PC_q), .clk(clock_1_out), .clr(in_8));
  Register AR (.D(adder_1_out), .en(in_5), .Q(AR_q), .clk(clock_1_out), .clr(in_8));
  Register MBR (.D(multiplexer_1_out), .Q(MBR_q), .clk(clock_1_out), .clr(in_8));  // open: en
  Multiplexer #(.width(8), .enable("false")) multiplexer_1 (
    .in0(adder_1_out), .in1(ram_1_data), .out(multiplexer_1_out), .sel(in_6));
  Register MAR (.D(adder_1_out), .Q(MAR_q), .clk(clock_1_out), .clr(in_8));  // open: en
  Register IR (.D(adder_1_out), .clk(clock_1_out), .clr(in_8));  // open: en, Q
  Multiplexer #(.select(2), .width(8), .enable("false")) multiplexer_2 (
    .in0(AC_q), .in1(PC_q), .in2(AR_q), .in3(MBR_q), .out(multiplexer_2_out), .sel(in_4));
  Multiplexer #(.select(2), .width(8), .enable("false")) multiplexer_3 (
    .in0(AC_q), .in1(PC_q), .in2(AR_q), .in3(MBR_q), .out(multiplexer_3_out), .sel(in_7));
  RAM ram_1 (.addr(MAR_q), .data(ram_1_data), .clk(clock_1_out));  // open: sel, ld, clr
  Adder adder_1 (.a(multiplexer_2_out), .b(multiplexer_3_out), .out(adder_1_out), .cin(in_2));  // open: cout
  Hex_Digit_Display hex_digit_display_1 (.value(adder_1_out[3:0]));  // open: dp
  Hex_Digit_Display hex_digit_display_2 (.value(adder_1_out[7:4]));  // open: dp
endmodule
