// Logisim project hw2-flipflop.circ as structural Verilog
module RS_Latch (
  input  S,
  input  R,
  output Q,
  output nQ
);

  nand nand_1 (Q, S, nQ);
  nand nand_2 (nQ, Q, R);
endmodule

// RS
module Clocked_RS_Latch (
  input  in_1,
  input  S,
  input  R,
  input  in_4,
  output Q,
  output nQ
);

  wire Ck_out, nand_1_out, nand_2_out;

  Clock Ck (.out(Ck_out));
  nand nand_1 (nand_1_out, S, Ck_out);
  nand nand_2 (nand_2_out, Ck_out, R);
  nand nand_3 (Q, in_1, nand_1_out, nQ);
  nand nand_4 (nQ, Q, nand_2_out, in_4);
endmodule

module D_flipflop (
  input  D,
  input  CK,
  output Q,
  output nQ
);

  wire clocked_rs_latch_1_p3;

  // Clocked_RS_Latch clocked_rs_latch_1: pin names not known; wires that end beside it: D, CK, clocked_rs_latch_1_p3, Q, nQ
  not not_1 (clocked_rs_latch_1_p3, D);
endmodule

module RS_Latch_NOR (
  input  in_1,
  input  in_2,
  output out_3,
  output out_4
);

  nor nor_1 (out_3, in_1, out_4);
  nor nor_2 (out_4, out_3, in_2);
endmodule

module register_test (
  input  [7:0] in_1,
  input  in_2,
  input  in_3,
  output [7:0] out_4
);

  wire clock_1_out;

  Register register_1 (.D(in_1), .en(in_2), .Q(out_4), .clk(clock_1_out), .clr(in_3));
  Clock clock_1 (.out(clock_1_out));
endmodule

module Clocked_RS_Latch_NOR (
  input  in_1,
  input  in_2,
  input  in_3,
  input  in_4,
  output out_5,
  output out_6
);

  wire and_1_out, and_2_out, clock_1_out;

  Clock clock_1 (.out(clock_1_out));
  and and_1 (and_1_out, in_2, clock_1_out);
  and and_2 (and_2_out, clock_1_out, in_3);
  nor nor_1 (out_5, in_1, and_1_out, out_6);
  nor nor_2 (out_6, out_5, and_2_out, in_4);
endmodule
